# Fritzing sketch Bluebomb-automator-gpio-wiring (saved by Fritzing 0.9.3b)
breadboards: 1

parts:
  Raspberry_Pi_2 = Raspberry Pi 4 [part_number=RPI-4-b]
  S1 = Pushbutton [package="[THT]"]
  S2 = Pushbutton [package="[THT]"]
  S3 = Pushbutton [package="[THT]"]
  LCD1 = LCD screen
  R1 = Resistor [tolerance=±5% resistance=2k package=THT]

nets:
  N1: Raspberry_Pi_2.GPIO2, S3.Pin_3, S3.Pin_4
  N2: Raspberry_Pi_2.GPIO3, S2.Pin_3, S2.Pin_4
  N3: Raspberry_Pi_2.GPIO4, S1.Pin_3, S1.Pin_4
  N4: Raspberry_Pi_2.GPIO22, LCD1.DB5
  N5: Raspberry_Pi_2.GPIO5, LCD1.RS
  N6: Raspberry_Pi_2.GPIO6, LCD1.E
  N7: Raspberry_Pi_2.GPIO21, LCD1.DB4
  N8: Raspberry_Pi_2.GPIO24, LCD1.DB7
  N9: Raspberry_Pi_2.GPIO23, LCD1.DB6
  GND: Raspberry_Pi_2.GND, S1.Pin_1, S1.Pin_2, S2.Pin_1, S2.Pin_2, S3.Pin_1, S3.Pin_2, LCD1.VSS, LCD1.R/W, LCD1.LED-, R1.Pin_1
  5V: Raspberry_Pi_2.5V, LCD1.VDD, LCD1.LED+
  N10: LCD1.V0, R1.Pin_0

custom parts:
  Raspberry Pi 4: The RPi4, a faster version of the awesome Raspberry Pi 2 B ARM Board with 40 pin gpio. Ready for special Raspberry Pi B+ and RPi2 Hat (Hardware attached (on) top)
