# Fritzing sketch Bluebomb-automator-wiring (saved by Fritzing 0.9.3b)

parts:
  Raspberry_Pi_1 = Raspberry Pi 4 [part_number=RPI-4-b]
  LCD1 = LCD screen
  LCM1602_IIC1 = LCM1602 IIC [part_number="LCM1602 IIC" chip_label="LCM1602 IIC" package="DIP (Dual Inline) [THT]"]
  S3 = Round Pushbutton
  S4 = Round Pushbutton
  S5 = Round Pushbutton

nets:
  3V3: Raspberry_Pi_1.3v3, LCM1602_IIC1.VCC
  N1: Raspberry_Pi_1.GPIO2, LCM1602_IIC1.SDA
  N2: Raspberry_Pi_1.GPIO3, LCM1602_IIC1.SCL
  N3: Raspberry_Pi_1.GPIO25, S5.leg0
  GND: Raspberry_Pi_1.GND, LCM1602_IIC1.GND, S3.leg1, S4.leg1, S5.leg1
  N4: Raspberry_Pi_1.GPIO24, S4.leg0
  N5: Raspberry_Pi_1.GPIO23, S3.leg0
  5V: Raspberry_Pi_1.5V, LCD1.VDD
  VSS: LCD1.VSS, LCM1602_IIC1.VSS
  N6: LCD1.V0, LCM1602_IIC1.V0
  N7: LCD1.RS, LCM1602_IIC1.RS
  N8: LCD1.R/W, LCM1602_IIC1.RW
  N9: LCD1.E, LCM1602_IIC1.E
  N10: LCD1.DB4, LCM1602_IIC1.D4
  N11: LCD1.DB5, LCM1602_IIC1.D5
  N12: LCD1.DB6, LCM1602_IIC1.D6
  N13: LCD1.DB7, LCM1602_IIC1.D7
  N14: LCD1.LED+, LCM1602_IIC1.A
  N15: LCD1.LED-, LCM1602_IIC1.K
  N16: LCM1602_IIC1.LED_A, LCM1602_IIC1.LED_B

custom parts:
  Raspberry Pi 4: The RPi4, a faster version of the awesome Raspberry Pi 2 B ARM Board with 40 pin gpio. Ready for special Raspberry Pi B+ and RPi2 Hat (Hardware attached (on) top)
  LCM1602 IIC: I2C-Module to use a 1602 or 2004 LCD on with the wire.h libory Serial LCD Modul
